# Fritzing sketch higrometro (saved by Fritzing 0.9.3b)
breadboards: 1

parts:
  Part13 = FC-28 Soil Hygrometer Module - Probe
  Part14 = FC-28 Soil Hygrometer Module
  Part15 = Arduino Uno (Rev3)
  LED3 = smd LED [color="Green (555nm)" package="0603 [SMD]"]
  LED4 = smd LED [color="Red (633nm)" package="0603 [SMD]"]
  R6 = Resistor [tolerance=±5% resistance=150 package=THT]
  R7 = Resistor [tolerance=±5% resistance=220 package=THT]

nets:
  N1: Part13.POS, Part14.POS
  N2: Part13.NEG, Part14.NEG
  N3: Part14.GND, LED3.cathode, LED4.cathode
  N4: Part14.AO, Part15.A1
  N5: Part15.D12/MISO, R7.Pin_1
  N6: Part15.D13/SCK, R6.Pin_1
  N7: LED3.anode, R7.Pin_0
  N8: LED4.anode, R6.Pin_0

custom parts:
  FC-28 Soil Hygrometer Module - Probe: The FC-28 is a soil hygrometer module that uses the Texas Instruments LM393 comparator chip to provide an analog measurement of soil humidity.
  FC-28 Soil Hygrometer Module: The FC-28 is a soil hygrometer module that uses the Texas Instruments LM393 comparator chip to provide an analog measurement of soil humidity. The digital output is high when soil moisture is over a certain threshold, as determined by adjusting the potentiometer.
