# Fritzing sketch BMP_180 (saved by Fritzing 0.9.2b)
breadboards: 1

parts:
  Part11 = Arduino Uno (Rev3)
  Part12 = Logic Level Converter
  SD_card_module4 = SD Card Module
  LCM1602_IIC5 = LCM1602 IIC [part_number="LCM1602 IIC" chip_label="LCM1602 IIC" package="DIP (Dual Inline) [THT]"]
  LCD5 = LCD screen

nets:
  N1: Part11.D11_PWM/MOSI, Part12.TX2_HV
  N2: Part11.D12/MISO, SD_card_module4.MISO
  N3: Part11.D13/SCK, Part12.TX_HV
  N4: Part11.A4/SDA, LCM1602_IIC5.SDA
  N5: Part11.A5/SCL, LCM1602_IIC5.SCL
  N6: Part11.D4, Part12.RX2_HV
  N7: Part11.3V3, Part12.LV
  5V: Part11.5V, LCM1602_IIC5.VCC
  GND: Part11.GND, Part12.GND, LCM1602_IIC5.GND
  N8: Part12.TX2_LV, SD_card_module4.MOSI
  N9: Part12.RX2_LV, SD_card_module4.CS
  N10: Part12.TX_LV, SD_card_module4.SCK
  VSS: LCM1602_IIC5.VSS, LCD5.VSS
  VDD: LCM1602_IIC5.VDD, LCD5.VDD
  N11: LCM1602_IIC5.V0, LCD5.V0
  N12: LCM1602_IIC5.RS, LCD5.RS
  N13: LCM1602_IIC5.RW, LCD5.R/W
  N14: LCM1602_IIC5.E, LCD5.E
  N15: LCM1602_IIC5.D0, LCD5.DB0
  N16: LCM1602_IIC5.D1, LCD5.DB1
  N17: LCM1602_IIC5.D2, LCD5.DB2
  N18: LCM1602_IIC5.D3, LCD5.DB3
  N19: LCM1602_IIC5.D4, LCD5.DB4
  N20: LCM1602_IIC5.D5, LCD5.DB5
  N21: LCM1602_IIC5.D6, LCD5.DB6
  N22: LCM1602_IIC5.D7, LCD5.DB7
  N23: LCM1602_IIC5.A, LCD5.LED+
  N24: LCM1602_IIC5.K, LCD5.LED-

custom parts:
  SD Card Module: SD Card Module Slot Socket Reader For Arduino ARM MCU
  LCM1602 IIC: I2C-Module to use a 1602 or 2004 LCD on with the wire.h libory Serial LCD Modul
